# Fritzing sketch Platine (saved by Fritzing 0.9.2b)
circuit board: 25cm x 1.2cm
circuit board: 7cm x 2.5cm
circuit board: 25cm x 1.2cm
circuit board: 25cm x 1.2cm
circuit board: 10.5cm x 10.5cm
circuit board: 25cm x 1.2cm
circuit board: 25cm x 25cm
breadboards: 1

parts:
  Pi_- = Pad [width=4.5 height=4.5 connect=center]
  Pi_PWM = Pad [width=4.5 height=4.5 connect=center]
  Pi_+ = Pad [width=4.5 height=4.5 connect=center]
  Bat_+ = Pad [width=4.5 height=4.5 connect=center]
  Bat_- = Pad [width=4.5 height=4.5 connect=center]
  X6 = USB Connectors [package=usb-a-s]
  X4 = USB Connectors [package=usb-a-s]
  X3 = USB Connectors [package=usb-a-s]
  X7 = USB Connectors [package=usb-a-s]
  X8 = USB Connectors [package=usb-microb]
  Lade_- = Pad [width=4.2499346405228602 height=4.31633986928105 connect=center]
  Lade_+ = Pad [width=4.2499346405228602 height=4.31633986928105 connect=center]
  Pi_Switch1 = Pad [width=4.5 height=4.5 connect=center]
  S1 = SPST Switch [package=switch-spdt-smd]
  Pad3 = Pad [width=10 height=3 connect=center]
  Standart = USB Connectors [package=usb-a-pcb]
  Pad4 = Pad [width=14.683352971309336 height=2.6581420646843741 connect=center]
  Pad6 = Pad [width=10 height=3 connect=center]
  Standart2 = USB Connectors [package=usb-a-pcb]
  Pad7 = Pad [width=10 height=3 connect=center]  # not connected
  Gespiegelt_mit_magnetschalter = USB Connectors [package=usb-a-pcb]
  Pad8 = Pad [width=2.2088635499809586 height=2.5010617002406983 connect=center]
  Pad9 = Pad [width=2.2088635499809586 height=2.5010617002406983 connect=center]
  Pad10 = Pad [width=2.2088635499809586 height=2.5010617002406983 connect=center]
  R1 = Resistor [tolerance=±5% resistance=1M package=THT]
  Pad11 = Pad [width=10 height=3 connect=center]
  Standart3 = USB Connectors [package=usb-a-pcb]
  Pad14 = Pad [width=15.481005190401669 height=2.5945291757955169 connect=center]
  Pad15 = Pad [width=15.481005190401669 height=2.5945291757955169 connect=center]
  Pad16 = Pad [width=14.683352971309336 height=2.6581420646843741 connect=center]
  Pad17 = Pad [width=15.481005190401669 height=2.5945291757955169 connect=center]
  Pad18 = Pad [width=15.481005190401669 height=2.5945291757955169 connect=center]
  Pad19 = Pad [width=14.683352971309336 height=2.6581420646843741 connect=center]
  Pad20 = Pad [width=15.481005190401669 height=2.5945291757955169 connect=center]
  Pad21 = Pad [width=15.481005190401669 height=2.5945291757955169 connect=center]
  Pad22 = Pad [width=14.683352971309336 height=2.6581420646843741 connect=center]
  Pad23 = Pad [width=15.481005190401669 height=2.5945291757955169 connect=center]
  Pad24 = Pad [width=15.481005190401669 height=2.5945291757955169 connect=center]

nets:
  N1: Pi_-.pad, Bat_-.pad, S1.O
  N2: Pi_PWM.pad, X7.D-
  GND: Pi_+.pad, Bat_+.pad, X6.GND, X4.VBUS, X3.GND, X7.VBUS
  N3: X6.D+, X7.D+
  N4: X6.D-, X4.D-
  GND_2: X6.VBUS, X4.GND, X3.VBUS, X7.GND, S1.P
  N5: X4.D+, X3.D-
  N6: X3.D+, Pi_Switch1.pad
  N7: X8.GND, Lade_-.pad
  N8: X8.VBUS, Lade_+.pad
  N9: Pad3.pad, Standart.D+
  N10: Standart.VBUS, Pad15.pad
  N11: Standart.GND, Pad14.pad
  N12: Standart.D-, Pad4.pad
  N13: Pad6.pad, Standart2.D-
  N14: Standart2.VBUS, Pad21.pad
  N15: Standart2.GND, Pad20.pad
  N16: Standart2.D+, Pad19.pad
  N17: Gespiegelt_mit_magnetschalter.VBUS, R1.Pin_0, Pad23.pad
  N18: Gespiegelt_mit_magnetschalter.GND, Pad9.pad, Pad24.pad
  N19: Gespiegelt_mit_magnetschalter.D-, Pad10.pad
  N20: Gespiegelt_mit_magnetschalter.D+, Pad22.pad
  N21: Pad8.pad, R1.Pin_1
  N22: Pad11.pad, Standart3.D+
  N23: Standart3.VBUS, Pad18.pad
  N24: Standart3.GND, Pad17.pad
  N25: Standart3.D-, Pad16.pad

notes:
  Usb gespiegelt
