# Fritzing sketch Schaltplan (saved by Fritzing 0.9.2b)
circuit board: 8.46667cm x 5.64444cm
stripboards: 1

parts:
  Raspberry_Pi1 = Raspberry Pi 2
  R1 = Resistor [tolerance=±5% resistance=220 package=THT]
  BAT2 = Battery Holders [package=battery-aa-panel]
  BAT3 = Battery Holders [package=battery-aa-panel]
  BAT4 = Battery Holders [package=battery-aa-panel]
  S3 = Reed switch [package=THT]
  LED_Streifen = ws2812b [package="smd 2812b"]
  R2 = Resistor [tolerance=±5% resistance=220 package=THT]
  BAT5 = Battery Holders [package=battery-aa-panel]
  BAT6 = Battery Holders [package=battery-aa-panel]
  BAT7 = Battery Holders [package=battery-aa-panel]
  BAT8 = Battery Holders [package=battery-aa-panel]
  BAT1 = Battery Holders [package=battery-aa-panel]

nets:
  N1: Raspberry_Pi1.GPIO17, S3.pin_1, R2.Pin_0
  GND: Raspberry_Pi1.GND, BAT2.-, LED_Streifen.VSS, R2.Pin_1, BAT6.-
  N2: Raspberry_Pi1.GPIO18, LED_Streifen.DIN
  N3: Raspberry_Pi1.5V, R1.Pin_0, BAT3.+, S3.pin_2, BAT7.+
  N4: R1.Pin_1, LED_Streifen.VDD
  N5: BAT2.+, BAT1.-
  N6: BAT3.-, BAT4.+
  N7: BAT4.-, BAT1.+
  N8: BAT5.+, BAT8.-
  N9: BAT5.-, BAT6.+
  N10: BAT7.-, BAT8.+
