# Fritzing sketch Schaltplan (saved by Fritzing 0.9.2b)
stripboards: 1

parts:
  Raspberry_Pi1 = Raspberry Pi 2
  R1 = Resistor [tolerance=±5% resistance=220 package=THT]
  BAT1 = Battery Holders [package=battery-aa-panel]
  BAT2 = Battery Holders [package=battery-aa-panel]
  BAT3 = Battery Holders [package=battery-aa-panel]
  BAT4 = Battery Holders [package=battery-aa-panel]
  S2 = SPST Switch [package=r_sw_th]
  S3 = Reed switch [package=THT]
  LED_Streifen = ws2812b [package="smd 2812b"]

nets:
  GND: Raspberry_Pi1.GND, Raspberry_Pi1.GPIO17, S2.O, S3.pin_1, LED_Streifen.VSS
  N1: Raspberry_Pi1.GPIO18, LED_Streifen.DIN
  N2: Raspberry_Pi1.5V, R1.Pin_0, BAT1.-, BAT2.+, BAT3.-, BAT4.+, S2.S
  N3: R1.Pin_1, S3.pin_2, LED_Streifen.VDD
  N4: BAT1.+, BAT2.-, BAT3.+, BAT4.-
